// Logisim project DDR.circ as structural Verilog: 1 circuit, main circuit main
module main (
  input  [3:0] Data,
  input  SendData,
  input  [3:0] Address,
  input  [3:0] in_4,
  input  in_5,
  input  in_6,
  input  in_7,
  input  in_8
);

  wire a1, a2, a3, a4, a5, a6, a7, a8, a9, a10, a11, a12, a13, a14, a15, a16, and_1_out, and_2_out,
       and_3_out, and_4_out, and_5_out, and_6_out, and_7_out, and_8_out, and_9_out, and_10_out, and_11_out,
       and_12_out, and_13_out, and_14_out, and_15_out, and_16_out, and_17_out, b1, b2, b3, b4, b5, b6, b7,
       b8, b9, b10, b11, b12, b13, b14, b15, b16, c1, c2, c3, c4, c5, c6, c7, c8, c9, c10, c11, c12, c13,
       c14, c15, c16, clock_1_out, clock_2_out, clock_3_out, clock_4_out, clock_5_out, clock_6_out,
       clock_7_out, clock_8_out, clock_9_out, clock_10_out, clock_11_out, clock_12_out, clock_13_out, d1, d2,
       d3, d4, d5, d6, d7, d8, d9, d10, d11, d12, d13, d14, d15, d16, demultiplexer_1_out0,
       demultiplexer_1_out1, demultiplexer_1_out2, demultiplexer_1_out3, demultiplexer_2_out0,
       demultiplexer_2_out1, demultiplexer_2_out2, demultiplexer_2_out3, demultiplexer_3_out0,
       demultiplexer_3_out1, demultiplexer_3_out2, demultiplexer_3_out3, demultiplexer_4_out0,
       demultiplexer_4_out1, demultiplexer_4_out2, demultiplexer_4_out3, demultiplexer_5_out0,
       demultiplexer_5_out1, demultiplexer_5_out2, demultiplexer_5_out3, demultiplexer_6_out0,
       demultiplexer_6_out1, demultiplexer_6_out2, demultiplexer_6_out3, multiplexer_6_out,
       multiplexer_7_out, multiplexer_8_out, multiplexer_9_out, not_1_out, not_2_out, not_3_out, not_4_out,
       or_1_out, or_2_out, or_3_out, or_4_out, or_5_out, pt_a, pt_b, pt_c, pt_d, shift_register_1_out,
       shift_register_2_out, shift_register_5_out, shift_register_6_out;
  wire [1:0] counter_2_q, counter_3_q, counter_4_q, counter_5_q;
  wire [3:0] _0_2_q, _0_3_q, _0_q, _1_2_q, _1_3_q, _1_q, _2_2_q, _2_3_q, _2_q, _3_2_q, _3_3_q, _3_q, _4_q,
       _5_q, _6_q, _7_q, adder_1_out, counter_1_q, demultiplexer_7_out0, demultiplexer_7_out1,
       demultiplexer_7_out2, demultiplexer_7_out3, demultiplexer_8_out0, demultiplexer_8_out1,
       demultiplexer_8_out2, demultiplexer_8_out3, demultiplexer_9_out0, demultiplexer_9_out1,
       demultiplexer_9_out2, demultiplexer_9_out3, demultiplexer_10_out0, demultiplexer_10_out1,
       demultiplexer_10_out2, demultiplexer_10_out3, multiplexer_1_out, multiplexer_2_out, multiplexer_3_out,
       multiplexer_4_out, multiplexer_5_out, register_1_q;

  Demultiplexer #(.select(2)) demultiplexer_1 (
    .out0(demultiplexer_1_out0), .out1(demultiplexer_1_out1), .out2(demultiplexer_1_out2),
    .out3(demultiplexer_1_out3), .in(1'b1), .sel(Address[3:2]));  // open: en
  Demultiplexer #(.select(2)) demultiplexer_2 (
    .out0(demultiplexer_2_out0), .out1(demultiplexer_2_out1), .out2(demultiplexer_2_out2),
    .out3(demultiplexer_2_out3), .in(1'b1), .sel(Address[3:2]));  // open: en
  and and_1 (and_1_out, SendData, 1'b1);
  Demultiplexer #(.select(2)) demultiplexer_3 (
    .out0(demultiplexer_3_out0), .out1(demultiplexer_3_out1), .out2(demultiplexer_3_out2),
    .out3(demultiplexer_3_out3), .in(and_1_out), .sel(Address[1:0]), .en(demultiplexer_1_out0));
  Demultiplexer #(.select(2)) demultiplexer_4 (
    .out0(demultiplexer_4_out0), .out1(demultiplexer_4_out1), .out2(demultiplexer_4_out2),
    .out3(demultiplexer_4_out3), .in(and_1_out), .sel(Address[1:0]), .en(demultiplexer_1_out1));
  Demultiplexer #(.select(2)) demultiplexer_5 (
    .out0(demultiplexer_5_out0), .out1(demultiplexer_5_out1), .out2(demultiplexer_5_out2),
    .out3(demultiplexer_5_out3), .in(and_1_out), .sel(Address[1:0]), .en(demultiplexer_1_out2));
  Demultiplexer #(.select(2)) demultiplexer_6 (
    .out0(demultiplexer_6_out0), .out1(demultiplexer_6_out1), .out2(demultiplexer_6_out2),
    .out3(demultiplexer_6_out3), .in(and_1_out), .sel(Address[1:0]), .en(demultiplexer_1_out3));
  Demultiplexer #(.select(2), .width(4)) demultiplexer_7 (
    .out0(demultiplexer_7_out0), .out1(demultiplexer_7_out1), .out2(demultiplexer_7_out2),
    .out3(demultiplexer_7_out3), .in(Data), .sel(Address[1:0]), .en(demultiplexer_2_out0));
  Demultiplexer #(.select(2), .width(4)) demultiplexer_8 (
    .out0(demultiplexer_8_out0), .out1(demultiplexer_8_out1), .out2(demultiplexer_8_out2),
    .out3(demultiplexer_8_out3), .in(Data), .sel(Address[1:0]), .en(demultiplexer_2_out1));
  Demultiplexer #(.select(2), .width(4)) demultiplexer_9 (
    .out0(demultiplexer_9_out0), .out1(demultiplexer_9_out1), .out2(demultiplexer_9_out2),
    .out3(demultiplexer_9_out3), .in(Data), .sel(Address[1:0]), .en(demultiplexer_2_out2));
  Demultiplexer #(.select(2), .width(4)) demultiplexer_10 (
    .out0(demultiplexer_10_out0), .out1(demultiplexer_10_out1), .out2(demultiplexer_10_out2),
    .out3(demultiplexer_10_out3), .in(Data), .sel(Address[1:0]), .en(demultiplexer_2_out3));
  Counter #(.width(4), .max('hf)) counter_1 (.Q(counter_1_q), .clk(clock_1_out));  // open: load, D, count, carry, clr
  Clock #(.highDuration(64), .lowDuration(64)) clock_1 (.out(clock_1_out));
  Register #(.width(4)) _3 (.D(demultiplexer_7_out3), .Q(_3_q), .clk(demultiplexer_3_out3));  // open: en, clr
  Register #(.width(4)) _7 (.D(demultiplexer_8_out3), .Q(_7_q), .clk(demultiplexer_4_out3));  // open: en, clr
  Register #(.width(4)) _3_2 (.D(demultiplexer_9_out3), .Q(_3_2_q), .clk(demultiplexer_5_out3));  // open: en, clr
  Register #(.width(4)) _3_3 (.D(demultiplexer_10_out3), .Q(_3_3_q), .clk(demultiplexer_6_out3));  // open: en, clr
  Register #(.width(4)) _2 (.D(demultiplexer_7_out2), .Q(_2_q), .clk(demultiplexer_3_out2));  // open: en, clr
  Register #(.width(4)) _6 (.D(demultiplexer_8_out2), .Q(_6_q), .clk(demultiplexer_4_out2));  // open: en, clr
  Register #(.width(4)) _2_2 (.D(demultiplexer_9_out2), .Q(_2_2_q), .clk(demultiplexer_5_out2));  // open: en, clr
  Register #(.width(4)) _2_3 (.D(demultiplexer_10_out2), .Q(_2_3_q), .clk(demultiplexer_6_out2));  // open: en, clr
  Register #(.width(4)) _1 (.D(demultiplexer_7_out1), .Q(_1_q), .clk(demultiplexer_3_out1));  // open: en, clr
  Register #(.width(4)) _5 (.D(demultiplexer_8_out1), .Q(_5_q), .clk(demultiplexer_4_out1));  // open: en, clr
  Register #(.width(4)) _1_2 (.D(demultiplexer_9_out1), .Q(_1_2_q), .clk(demultiplexer_5_out1));  // open: en, clr
  Register #(.width(4)) _1_3 (.D(demultiplexer_10_out1), .Q(_1_3_q), .clk(demultiplexer_6_out1));  // open: en, clr
  Register #(.width(4)) _0 (.D(demultiplexer_7_out0), .Q(_0_q), .clk(demultiplexer_3_out0));  // open: en, clr
  Register #(.width(4)) _4 (.D(demultiplexer_8_out0), .Q(_4_q), .clk(demultiplexer_4_out0));  // open: en, clr
  Register #(.width(4)) _0_2 (.D(demultiplexer_9_out0), .Q(_0_2_q), .clk(demultiplexer_5_out0));  // open: en, clr
  Register #(.width(4)) _0_3 (.D(demultiplexer_10_out0), .Q(_0_3_q), .clk(demultiplexer_6_out0));  // open: en, clr
  Multiplexer #(.select(2), .width(4)) multiplexer_1 (
    .in0(_0_q), .in1(_1_q), .in2(_2_q), .in3(_3_q), .out(multiplexer_1_out), .sel(counter_1_q[1:0]));  // open: en
  Multiplexer #(.select(2), .width(4)) multiplexer_2 (
    .in0(_4_q), .in1(_5_q), .in2(_6_q), .in3(_7_q), .out(multiplexer_2_out), .sel(counter_1_q[1:0]));  // open: en
  Multiplexer #(.select(2), .width(4)) multiplexer_3 (
    .in0(_0_2_q), .in1(_1_2_q), .in2(_2_2_q), .in3(_3_2_q), .out(multiplexer_3_out), .sel(counter_1_q[1:0]));  // open: en
  Multiplexer #(.select(2), .width(4)) multiplexer_4 (
    .in0(_0_3_q), .in1(_1_3_q), .in2(_2_3_q), .in3(_3_3_q), .out(multiplexer_4_out), .sel(counter_1_q[1:0]));  // open: en
  Multiplexer #(.select(2), .width(4)) multiplexer_5 (
    .in0(multiplexer_1_out), .in1(multiplexer_2_out), .in2(multiplexer_3_out), .in3(multiplexer_4_out),
    .out(multiplexer_5_out), .sel(counter_1_q[3:2]));  // open: en
  and and_2 (and_2_out, in_5, clock_2_out);
  Clock clock_2 (.out(clock_2_out));
  Multiplexer multiplexer_6 (.in0(clock_3_out), .in1(clock_2_out), .out(multiplexer_6_out), .sel(pt_a));  // open: en
  Shift_Register shift_register_1 (
    .in(multiplexer_5_out[0]), .clk(clock_3_out), .out(shift_register_1_out), .clr(or_1_out), .q0(a1),
    .q1(a2), .q2(a3), .q3(a4), .q4(a5), .q5(a6), .q6(a7), .q7(a8));  // open: shift, load, d0, d1, d2, d3, d4, d5, d6, d7
  Clock #(.highDuration(64), .lowDuration(64)) clock_3 (.out(clock_3_out));
  and and_3 (and_3_out, in_6, clock_4_out);
  Clock clock_4 (.out(clock_4_out));
  Multiplexer multiplexer_7 (.in0(clock_5_out), .in1(clock_4_out), .out(multiplexer_7_out), .sel(pt_b));  // open: en
  Shift_Register shift_register_2 (
    .in(multiplexer_5_out[1]), .clk(clock_5_out), .out(shift_register_2_out), .clr(or_2_out), .q0(b1),
    .q1(b2), .q2(b3), .q3(b4), .q4(b5), .q5(b6), .q6(b7), .q7(b8));  // open: shift, load, d0, d1, d2, d3, d4, d5, d6, d7
  Clock #(.highDuration(64), .lowDuration(64)) clock_5 (.out(clock_5_out));
  D_Flip_Flop d_ff_1 (.clk(and_2_out), .D(a15), .Q(pt_a));  // open: Qn, preset, en, reset
  D_Flip_Flop d_ff_2 (.clk(and_3_out), .D(b15), .Q(pt_b));  // open: Qn, preset, en, reset
  Shift_Register shift_register_3 (
    .in(shift_register_1_out), .clk(multiplexer_6_out), .load(pt_a), .clr(or_1_out), .d0(a9), .q0(a9),
    .d1(a10), .q1(a10), .d2(a11), .q2(a11), .d3(a12), .q3(a12), .d4(a13), .q4(a13), .d5(a14), .q5(a14),
    .d6(1'b0), .q6(a15), .d7(a16), .q7(a16));  // open: shift, out
  Shift_Register shift_register_4 (
    .in(shift_register_2_out), .clk(multiplexer_7_out), .load(pt_b), .clr(or_2_out), .d0(b9), .q0(b9),
    .d1(b10), .q1(b10), .d2(b11), .q2(b11), .d3(b12), .q3(b12), .d4(b13), .q4(b13), .d5(b14), .q5(b14),
    .d6(1'b0), .q6(b15), .d7(b16), .q7(b16));  // open: shift, out
  LED led_1 (.in(b1));
  LED led_2 (.in(a1));
  LED led_3 (.in(a2));
  LED led_4 (.in(b2));
  LED led_5 (.in(a3));
  LED led_6 (.in(b3));
  LED led_7 (.in(b4));
  LED led_8 (.in(a4));
  LED led_9 (.in(b5));
  LED led_10 (.in(a5));
  LED led_11 (.in(b6));
  LED led_12 (.in(a6));
  LED led_13 (.in(b7));
  LED led_14 (.in(a7));
  LED led_15 (.in(b8));
  LED led_16 (.in(a8));
  LED led_17 (.in(a9));
  LED led_18 (.in(b9));
  LED led_19 (.in(a10));
  LED led_20 (.in(b10));
  LED led_21 (.in(a11));
  LED led_22 (.in(b11));
  LED led_23 (.in(a12));
  LED led_24 (.in(b12));
  LED led_25 (.in(a13));
  LED led_26 (.in(b13));
  LED led_27 (.in(a14));
  LED led_28 (.in(b14));
  LED led_29 (.in(a15));
  LED led_30 (.in(b15));
  LED led_31 (.in(b16));
  LED led_32 (.in(a16));
  LED led_33 (.in(d1));
  LED led_34 (.in(c1));
  LED led_35 (.in(c2));
  LED led_36 (.in(d2));
  LED led_37 (.in(c3));
  LED led_38 (.in(d3));
  LED led_39 (.in(d4));
  LED led_40 (.in(c4));
  LED led_41 (.in(c5));
  LED led_42 (.in(d5));
  LED led_43 (.in(d6));
  LED led_44 (.in(c6));
  LED led_45 (.in(d7));
  LED led_46 (.in(c7));
  LED led_47 (.in(c8));
  LED led_48 (.in(d8));
  LED led_49 (.in(d9));
  LED led_50 (.in(c9));
  LED led_51 (.in(d10));
  LED led_52 (.in(c10));
  LED led_53 (.in(c11));
  LED led_54 (.in(d11));
  LED led_55 (.in(c12));
  LED led_56 (.in(d12));
  LED led_57 (.in(d13));
  LED led_58 (.in(c13));
  LED led_59 (.in(d14));
  LED led_60 (.in(c14));
  LED led_61 (.in(c15));
  LED led_62 (.in(d15));
  LED led_63 (.in(c16));
  LED led_64 (.in(d16));
  Counter #(.width(2), .max('h3)) counter_2 (
    .Q(counter_2_q), .clk(and_4_out), .clr(not_1_out));  // open: load, D, count, carry
  not not_1 (not_1_out, in_5);
  and and_4 (and_4_out, in_5, clock_6_out);
  Clock #(.highDuration(5), .lowDuration(5)) clock_6 (.out(clock_6_out));
  Counter #(.width(2), .max('h3)) counter_3 (
    .Q(counter_3_q), .clk(and_5_out), .clr(not_2_out));  // open: load, D, count, carry
  not not_2 (not_2_out, in_6);
  and and_5 (and_5_out, in_6, clock_7_out);
  Clock #(.highDuration(5), .lowDuration(5)) clock_7 (.out(clock_7_out));
  and and_6 (and_6_out, a15, in_5);
  and and_7 (and_7_out, b15, in_6);
  and and_8 (and_8_out, c15, in_7);
  buf and_9 (and_9_out, d15);  // AND_Gate
  and and_10 (and_10_out, counter_2_q[1], counter_2_q[0]);
  or or_1 (or_1_out, a16, and_10_out);
  and and_11 (and_11_out, counter_3_q[1], counter_3_q[0]);
  or or_2 (or_2_out, b16, and_11_out);
  or or_3 (or_3_out, and_6_out, and_7_out, and_8_out, and_9_out);
  Clock clock_8 (.out(clock_8_out));
  Clock #(.highDuration(64), .lowDuration(64)) clock_9 (.out(clock_9_out));
  Clock clock_10 (.out(clock_10_out));
  Clock #(.highDuration(64), .lowDuration(64)) clock_11 (.out(clock_11_out));
  Register #(.width(4)) register_1 (.D(adder_1_out), .Q(register_1_q), .clk(or_3_out));  // open: en, clr
  and and_12 (and_12_out, in_7, clock_8_out);
  Multiplexer multiplexer_8 (.in0(clock_9_out), .in1(clock_8_out), .out(multiplexer_8_out), .sel(pt_c));  // open: en
  Shift_Register shift_register_5 (
    .in(multiplexer_5_out[2]), .clk(clock_9_out), .out(shift_register_5_out), .clr(or_4_out), .q0(c1),
    .q1(c2), .q2(c3), .q3(c4), .q4(c5), .q5(c6), .q6(c7), .q7(c8));  // open: shift, load, d0, d1, d2, d3, d4, d5, d6, d7
  and and_13 (and_13_out, in_8, clock_10_out);
  Multiplexer multiplexer_9 (.in0(clock_11_out), .in1(clock_10_out), .out(multiplexer_9_out), .sel(pt_d));  // open: en
  Shift_Register shift_register_6 (
    .in(multiplexer_5_out[3]), .clk(clock_11_out), .out(shift_register_6_out), .clr(or_5_out), .q0(d1),
    .q1(d2), .q2(d3), .q3(d4), .q4(d5), .q5(d6), .q6(d7), .q7(d8));  // open: shift, load, d0, d1, d2, d3, d4, d5, d6, d7
  LED Points (.in(register_1_q[0]));
  LED led_65 (.in(register_1_q[1]));
  LED led_66 (.in(register_1_q[2]));
  LED led_67 (.in(register_1_q[3]));
  Adder #(.width(4)) adder_1 (.a(in_4), .b(register_1_q), .out(adder_1_out));  // open: cin, cout
  D_Flip_Flop d_ff_3 (.clk(and_12_out), .D(c15), .Q(pt_c));  // open: Qn, preset, en, reset
  D_Flip_Flop d_ff_4 (.clk(and_13_out), .D(d15), .Q(pt_d));  // open: Qn, preset, en, reset
  Shift_Register shift_register_7 (
    .in(shift_register_5_out), .clk(multiplexer_8_out), .load(pt_c), .clr(or_4_out), .d0(c9), .q0(c9),
    .d1(c10), .q1(c10), .d2(c11), .q2(c11), .d3(c12), .q3(c12), .d4(c13), .q4(c13), .d5(c14), .q5(c14),
    .d6(1'b0), .q6(c15), .d7(c16), .q7(c16));  // open: shift, out
  Shift_Register shift_register_8 (
    .in(shift_register_6_out), .clk(multiplexer_9_out), .load(pt_d), .clr(or_5_out), .d0(d9), .q0(d9),
    .d1(d10), .q1(d10), .d2(d11), .q2(d11), .d3(d12), .q3(d12), .d4(d13), .q4(d13), .d5(d14), .q5(d14),
    .d6(1'b0), .q6(d15), .d7(d16), .q7(d16));  // open: shift, out
  Counter #(.width(2), .max('h3)) counter_4 (
    .Q(counter_4_q), .clk(and_14_out), .clr(not_3_out));  // open: load, D, count, carry
  not not_3 (not_3_out, in_7);
  and and_14 (and_14_out, in_7, clock_12_out);
  Clock #(.highDuration(5), .lowDuration(5)) clock_12 (.out(clock_12_out));
  or or_4 (or_4_out, c16, and_16_out);
  Counter #(.width(2), .max('h3)) counter_5 (
    .Q(counter_5_q), .clk(and_15_out), .clr(not_4_out));  // open: load, D, count, carry
  not not_4 (not_4_out, in_8);
  and and_15 (and_15_out, in_8, clock_13_out);
  Clock #(.highDuration(5), .lowDuration(5)) clock_13 (.out(clock_13_out));
  or or_5 (or_5_out, d16, and_17_out);
  and and_16 (and_16_out, counter_4_q[1], counter_4_q[0]);
  and and_17 (and_17_out, counter_5_q[1], counter_5_q[0]);
  BitSelector bitselector_1 ();  // open: in, out, sel

  // Notes on the sheet:
  //   It should odejmowac points when you hit an empty ball
endmodule
